// Logisim project AbAd12.circ as structural Verilog: 1 circuit, main circuit main
module main (
  input  [3:0] in_1,
  input  [3:0] in_2,
  input  [3:0] in_3,
  input  [3:0] in_4,
  input  [3:0] in_5,
  input  [3:0] in_6,
  input  [3:0] in_7,
  input  [3:0] in_8,
  input  [3:0] A,
  input  [3:0] B,
  output [3:0] EVEN,
  output [3:0] ODD
);

  wire [3:0] and_1_out, and_2_out, and_3_out, and_4_out, not_1_out, not_2_out, not_3_out, not_4_out,
       not_5_out, not_6_out, not_7_out, not_8_out, not_9_out, not_10_out, undriven, xor_1_out, xor_2_out,
       xor_3_out, xor_4_out, xor_5_out, xor_6_out, xor_7_out;

  assign xor_1_out = in_1 ^ in_2;  // XOR_Gate xor_1, 4 bits wide
  assign not_1_out = ~xor_1_out;  // NOT_Gate not_1, 4 bits wide
  assign xor_2_out = in_3 ^ in_4;  // XOR_Gate xor_2, 4 bits wide
  assign not_2_out = ~xor_2_out;  // NOT_Gate not_2, 4 bits wide
  assign xor_3_out = in_5 ^ in_6;  // XOR_Gate xor_3, 4 bits wide
  assign not_3_out = ~xor_3_out;  // NOT_Gate not_3, 4 bits wide
  assign xor_4_out = in_7 ^ in_8;  // XOR_Gate xor_4, 4 bits wide
  assign not_4_out = ~xor_4_out;  // NOT_Gate not_4, 4 bits wide
  assign xor_5_out = not_3_out ^ not_4_out;  // XOR_Gate xor_5, 4 bits wide
  assign xor_6_out = not_1_out ^ not_2_out;  // XOR_Gate xor_6, 4 bits wide
  assign xor_7_out = xor_6_out ^ xor_5_out;  // XOR_Gate xor_7, 4 bits wide
  assign not_5_out = ~xor_7_out;  // NOT_Gate not_5, 4 bits wide
  assign not_6_out = ~not_5_out;  // NOT_Gate not_6, 4 bits wide
  assign and_1_out = undriven & A;  // AND_Gate and_1, 4 bits wide
  assign and_2_out = not_6_out & B;  // AND_Gate and_2, 4 bits wide
  assign and_3_out = B & undriven;  // AND_Gate and_3, 4 bits wide
  assign and_4_out = not_6_out & A;  // AND_Gate and_4, 4 bits wide
  assign not_7_out = ~and_1_out;  // NOT_Gate not_7, 4 bits wide
  assign not_8_out = ~and_2_out;  // NOT_Gate not_8, 4 bits wide
  assign not_9_out = ~and_3_out;  // NOT_Gate not_9, 4 bits wide
  assign not_10_out = ~and_4_out;  // NOT_Gate not_10, 4 bits wide
  assign EVEN = not_7_out & not_8_out;  // AND_Gate and_5, 4 bits wide
  assign ODD = not_9_out & not_10_out;  // AND_Gate and_6, 4 bits wide
endmodule
